# Fritzing sketch Schaltung (saved by Fritzing 1.0.3b)
circuit board: 8.46667cm x 5.64444cm
breadboards: 1

parts:
  Bauteil1 = Arduino Nano (Rev3.0)
  LCM1602_IIC1 = LCM1602 IIC [part_number="LCM1602 IIC" chip_label="LCM1602 IIC" package="DIP (Dual Inline) [THT]"]
  S2 = Pushbutton [package="[THT]"]
  R1 = Resistor [tolerance=±5% power=0.25W resistance=10k package=THT]
  R2 = Resistor [tolerance=±5% power=0.25W resistance=10k package=THT]
  J1 = male pin header, 4 pins [form="♂ (male)"]
  4x20_LCD_screen_w/Red_Screen1 = 4x20 LCD screen w/Red Screen
  S3 = Pushbutton [package="[THT]"]

nets:
  GND: Bauteil1.GND, LCM1602_IIC1.GND, R1.Pin_0, R2.Pin_0, J1.pin1
  VIN: Bauteil1.D2, Bauteil1.D3, Bauteil1.VIN, LCM1602_IIC1.VCC, S2.Pin_1, S2.Pin_2, S2.Pin_3, S2.Pin_4, R1.Pin_1, R2.Pin_1, J1.pin2, S3.Pin_1, S3.Pin_2, S3.Pin_3, S3.Pin_4
  N1: Bauteil1.A6, Bauteil1.A5, LCM1602_IIC1.SCL, J1.pin4
  N2: Bauteil1.A4, LCM1602_IIC1.SDA, J1.pin3
  VSS: LCM1602_IIC1.VSS, 4x20_LCD_screen_w/Red_Screen1.VSS
  VDD: LCM1602_IIC1.VDD, 4x20_LCD_screen_w/Red_Screen1.VDD
  N3: LCM1602_IIC1.V0, 4x20_LCD_screen_w/Red_Screen1.V0
  N4: LCM1602_IIC1.RS, 4x20_LCD_screen_w/Red_Screen1.RS
  N5: LCM1602_IIC1.RW, 4x20_LCD_screen_w/Red_Screen1.R/W
  N6: LCM1602_IIC1.E, 4x20_LCD_screen_w/Red_Screen1.E
  N7: LCM1602_IIC1.D0, 4x20_LCD_screen_w/Red_Screen1.DB0
  N8: LCM1602_IIC1.D1, 4x20_LCD_screen_w/Red_Screen1.DB1
  N9: LCM1602_IIC1.D2, 4x20_LCD_screen_w/Red_Screen1.DB2
  N10: LCM1602_IIC1.D3, 4x20_LCD_screen_w/Red_Screen1.DB3
  N11: LCM1602_IIC1.D4, 4x20_LCD_screen_w/Red_Screen1.DB4
  N12: LCM1602_IIC1.D5, 4x20_LCD_screen_w/Red_Screen1.DB5
  N13: LCM1602_IIC1.D6, 4x20_LCD_screen_w/Red_Screen1.DB6
  N14: LCM1602_IIC1.D7, 4x20_LCD_screen_w/Red_Screen1.DB7
  N15: LCM1602_IIC1.A, 4x20_LCD_screen_w/Red_Screen1.LED+
  N16: LCM1602_IIC1.K, 4x20_LCD_screen_w/Red_Screen1.LED-

custom parts:
  LCM1602 IIC: I2C-Module to use a 1602 or 2004 LCD on with the wire.h libory Serial LCD Modul
  4x20 LCD screen w/Red Screen: A standard character display with 4x20 characters.
